# Fritzing sketch Ultrasonic sensor (saved by Fritzing 0.9.3b)
breadboards: 1

parts:
  Part1 = Arduino Leonardo (Rev3b)
  hc-sr1 = hc-sr04
  LED1 = LED - 5mm [color="Red (633nm)" package="5 mm [THT]"]

nets:
  5V: Part1.5V, hc-sr1.VCC
  GND: Part1.GND, hc-sr1.GND, LED1.cathode
  N1: Part1.D10_PWM/A10, hc-sr1.Echo
  N2: Part1.D11_PWM, hc-sr1.Trig
  N3: Part1.D13_PWM, LED1.anode
